# Fritzing sketch Breadboard (saved by Fritzing 0.9.4)
circuit board: 7.28645cm x 5.11054cm
breadboards: 1

parts:
  WiFi = ESP8266 WiFi Module [part_number=ESP8266]
  220OHM = Resistor [tolerance=±5% resistance=220 package=THT]
  220ohm = Resistor [tolerance=±5% resistance=220 package=THT]
  220ohm_2 = Resistor [tolerance=±5% resistance=220 package=THT]
  Arduino_Nano_v3 = Arduino Nano (Rev3.0)
  100nf = Electrolytic Capacitor [capacitance=100nF package="100 mil [THT, electrolytic]"]
  10uf = Electrolytic Capacitor [capacitance=10µF package="100 mil [THT, electrolytic]"]
  100nf_2 = Electrolytic Capacitor [capacitance=100nF package="100 mil [THT, electrolytic]"]
  9V = Battery block 9V
  9v = Power Jack [package=power_jack_pth]
  LD1117V33 = V_REG_LD1117VXX [package=78xxl]
  Temp = female pin header, 4 pins [form="♀ (female)"]
  Display = female pin header, 4 pins [form="♀ (female)"]
  LD1117V50 = V_REG_LD1117VXX [package=78xxl]
  10uf_2 = Electrolytic Capacitor [capacitance=10µF package="100 mil [THT, electrolytic]"]

nets:
  N1: WiFi.RXD, 220ohm.Pin_1, 220ohm_2.Pin_0
  N2: WiFi.VCC, WiFi.CH_PD, 10uf.+, LD1117V33.OUT
  GND: WiFi.GND, 220OHM.Pin_0, Arduino_Nano_v3.GND, 100nf.-, 10uf.-, 100nf_2.-, 9V.-, 9v.GND, LD1117V33.GND, Temp.pin3, Display.pin3, LD1117V50.GND, 10uf_2.-
  N3: WiFi.TXD, Arduino_Nano_v3.D6
  N4: 220OHM.Pin_1, 220ohm.Pin_0
  N5: 220ohm_2.Pin_1, Arduino_Nano_v3.D7
  N6: Arduino_Nano_v3.VIN, 100nf.+, 100nf_2.+, 9V.+, 9v.PWR, LD1117V33.IN, LD1117V50.IN
  N7: Arduino_Nano_v3.A5, Temp.pin2, Display.pin2
  N8: Arduino_Nano_v3.A4, Temp.pin1, Display.pin1
  N9: Temp.pin4, Display.pin4, LD1117V50.OUT, 10uf_2.+

notes:
  Environment Monitor v1
  Designed by Sam Pratt
  SDA SCL GND 5V
  + -
  GND
  PWR
  TX RX
  SDA SCL
  GND VIN
  GND      RX
  TX EN  VCC
  GND OUT IN
  IN OUT GND

custom parts:
  ESP8266 WiFi Module: Generic WiFi Module based on the ESP8266 with onboard PCB antenna and UART communications
